// Digital circuit CPU.dig as structural Verilog
module CPU (
  input  RST,
  input  CLK,
  input  clk_2,
  input  CLK_SEL,
  output [7:0] opcode,
  output [15:0] rom,
  output [3:0] step
);

  wire A_LD, A_OE, A_SEL, addr_dec_1_p2, addr_dec_1_p3, alu_1_c_flag, alu_1_n_flag, alu_1_v_flag,
       alu_1_z_flag, ALU_CIN, ALU_S0, ALU_S1, ALU_S2, and_1_out, and_2_out, C, CLK_t, FL_SEL, K_av, MAR_DIR,
       MEM_RD, MEM_WR, mmio_1_p10, N, nALU_OE, nFL_LD, nFL_OE, nHBA_OE, nIR_LD, nIRA_OE, nIRD_OE, nMAR_INC,
       nMAR_OE, nMARH_LD, nMARL_LD, nMMIO_CS, nMPC_RST, nPC_LD, nPCH_OE, nPCL_OE, nRST, nSHR, nSP_INC,
       nSP_LD, nSP_OE, nSPH_OE, nSPL_OE, nXY_AOE, nXY_INC, PC_INC, PC_OE, REG_LD, REG_OE, SHR_IN0, SP_DIR,
       SRC_SEL, V, XY_DIR, Z;
  wire [2:0] Rsrc;
  wire [3:0] mmio_1_p8;
  wire [7:0] a_h__buffer_1_a_h__bus, alu_1_alu, mmio_1_p6, mmio_1_p9, pc_1_p10, rst_buffer_1_a_bus;
  wire [15:8] ctrlunit_1_c32_47, keyboard_1_d;

  not not_1 (nRST, RST);
  and and_1 (and_1_out, CLK, ~CLK_SEL);  // And
  and and_2 (and_2_out, CLK_SEL, clk_2);
  or or_1 (CLK_t, and_1_out, and_2_out);
  A_H__BUFFER a_h__buffer_1 (.nHBA_OE(nHBA_OE), .A_H__BUS(a_h__buffer_1_a_h__bus));
  RST_Buffer rst_buffer_1 (.RST(nRST), .A_BUS({a_h__buffer_1_a_h__bus, rst_buffer_1_a_bus}));
  // ADDR_DEC addr_dec_1: pin names not known; wires that end beside it: {a_h__buffer_1_a_h__bus, rst_buffer_1_a_bus}, addr_dec_1_p2, addr_dec_1_p3, nMMIO_CS
  // PC pc_1: pin names not known; wires that end beside it: {a_h__buffer_1_a_h__bus, rst_buffer_1_a_bus}, PC_INC, nPC_LD, PC_OE, nPCL_OE, nPCH_OE, CLK_t, RST, {a_h__buffer_1_a_h__bus, rst_buffer_1_a_bus}, pc_1_p10
  // SP sp_1: pin names not known; wires that end beside it: {a_h__buffer_1_a_h__bus, rst_buffer_1_a_bus}, nSP_INC, SP_DIR, nSP_LD, nSP_OE, nSPH_OE, nSPL_OE, CLK_t
  // MAR mar_1: pin names not known; wires that end beside it: {a_h__buffer_1_a_h__bus, rst_buffer_1_a_bus}, CLK_t, MAR_DIR, nMAR_INC, nMAR_OE, nMARH_LD, nMARL_LD, pc_1_p10, {a_h__buffer_1_a_h__bus, rst_buffer_1_a_bus}, pc_1_p10
  RAMSinglePortSel #(.AddrBits(16), .Bits(8)) ramsingleportsel_1 (
    .A({a_h__buffer_1_a_h__bus, rst_buffer_1_a_bus}), .CS(~addr_dec_1_p2), .WE(MEM_WR), .OE(MEM_RD),
    .D(pc_1_p10));
  EEPROM #(.AddrBits(15), .Bits(16)) eeprom_1 (
    .A({1'b0, a_h__buffer_1_a_h__bus[5:0], rst_buffer_1_a_bus}), .CS(~addr_dec_1_p3), .WE(1'b0), .OE(MEM_RD),
    .D(rom));
  RFILE rfile_1 (
    .DB_IN(pc_1_p10), .B_10_8(opcode[2:0]), .B_7_5(Rsrc), .REG_LD_EN(REG_LD), .REG_OE_EN(REG_OE),
    .nXY_INC(nXY_INC), .XY_DIR(XY_DIR), .nXY_AOE(nXY_AOE), .SRC_SEL(SRC_SEL), .CLK(CLK_t), .RST(RST),
    .DB_OUT(pc_1_p10), .AB_OUT({a_h__buffer_1_a_h__bus, rst_buffer_1_a_bus}), .A_LD(A_LD), .A_OE(A_OE));
  ALU alu_1 (
    .D_IN(pc_1_p10), .A_LD(A_LD), .A_OE(A_OE), .A_SEL(A_SEL), .ALU_S0(ALU_S0), .ALU_S1(ALU_S1),
    .ALU_S2(ALU_S2), .nALU_OE(nALU_OE), .ALU_CIN(ALU_CIN), .nSHR(nSHR), .SHR_IN0(SHR_IN0), .CLK(CLK_t),
    .RST(RST), .ALU(alu_1_alu), .Z_FLAG(alu_1_z_flag), .C_FLAG(alu_1_c_flag), .N_FLAG(alu_1_n_flag),
    .V_FLAG(alu_1_v_flag), .A_R_OUT(pc_1_p10));
  IR ir_1 (
    .ROM_IN(rom), .nIRH_LD(nIR_LD), .nIRL_LD(nIRD_OE), .nIRD_OE(nIRA_OE), .nIRA_OE(CLK_t),
    ._15_11(opcode[7:3]), ._10_8(opcode[2:0]), ._7_5(Rsrc), ._0_7(pc_1_p10), .AB(rst_buffer_1_a_bus));  // open: CLK
  microPC micropc_1 (.CLK(CLK_t), .nMPC_RST(nMPC_RST), .microstep(step));
  // MMIO mmio_1: pin names not known; wires that end beside it: {a_h__buffer_1_a_h__bus, rst_buffer_1_a_bus}, pc_1_p10, nMMIO_CS, MEM_WR, MEM_RD, mmio_1_p6, pc_1_p10, mmio_1_p8, mmio_1_p9, mmio_1_p10
  STATUS_REG status_reg_1 (
    .D_IN(alu_1_alu), .Z_FLAG(alu_1_z_flag), .C_FLAG(alu_1_c_flag), .N_FLAG(alu_1_n_flag),
    .V_FLAG(alu_1_v_flag), .nFL_OE(nFL_OE), .nFL_LD(nFL_LD), .FL_SEL(FL_SEL), .CLK(CLK_t), .nRST(nRST),
    .D_OUT(pc_1_p10), .Z(Z), .C(C), .N(N), .V(V));
  CTRLUNIT ctrlunit_1 (
    .OPC(opcode), .microstep(step), .Z(Z), .C(C), .N(N), .V(V),
    .C0_15({nMAR_INC, nMAR_OE, nMARH_LD, nMARL_LD, MEM_WR, MEM_RD, nMPC_RST, nHBA_OE, nIRA_OE, nIRD_OE, nIR_LD, nPCH_OE, nPCL_OE, PC_OE, nPC_LD, PC_INC}),
    .C16_31({nFL_LD, nFL_OE, SHR_IN0, nSHR, ALU_CIN, nALU_OE, ALU_S2, ALU_S1, ALU_S0, A_SEL, nXY_AOE, XY_DIR, nXY_INC, REG_OE, REG_LD, MAR_DIR}),
    .C32_47({ctrlunit_1_c32_47, SRC_SEL, nSPH_OE, nSPL_OE, nSP_OE, nSP_LD, SP_DIR, nSP_INC, FL_SEL}));
  Keyboard keyboard_1 (.C(mmio_1_p10), .en(1'b1), .D({keyboard_1_d, mmio_1_p6}), .av(K_av));
  LED SCLK (.in(mmio_1_p8[0]));
  LED SDIN (.in(mmio_1_p8[1]));
  LED DC (.in(mmio_1_p8[2]));
  LED CS (.in(mmio_1_p8[3]));
  LED led_1 (.in(mmio_1_p9[0]));
  LED led_2 (.in(mmio_1_p9[1]));
  LED led_3 (.in(mmio_1_p9[2]));
  LED led_4 (.in(mmio_1_p9[3]));
  LED led_5 (.in(mmio_1_p9[4]));
  LED led_6 (.in(mmio_1_p9[5]));
  LED led_7 (.in(mmio_1_p9[6]));
  LED led_8 (.in(mmio_1_p9[7]));

  // Other names for the same wires on the sheet: Rdst[2:0] = opcode[2:0]

  // Notes on the sheet:
  //   clk_2: Hz: 10
  //   contents of eeprom_1 (hex, n*v repeats v):
  //   601,5,d006,dac0,da5c,602,a800,d006,dbc0,db5c,dac0,da0e,e8c0,e85c
  //   ,11,122,233,344,455,566,677,788,3825,394a,3a6f,3b93,3cb6,3ddc
  //   ,3eff,3f00,603,2025,d011,dbc0,db5c,604,204a,d022,dbc0,db5c,605
  //   ,206f,d033,dbc0,db5c,606,2093,d044,dbc0,db5c,607,20b6,d055,dbc0
  //   ,db5c,608,20dc,d066,dbc0,db5c,609,20ff,d077,dbc0,db5c,60a,2100
  //   ,820,d088,dbc0,db5c,5a,1a5,1600,1a00,ee00,f500,f800,fa00,fb00
  //   ,fc00,60b,d05a,dbc0,db5c,60c,820,d0a5,dbc0,db5c,e8c0,e85a,e8c0,e85c
endmodule
